# Fritzing sketch MFC-fcm-wiring-schematic (saved by Fritzing 0.9.4)
breadboards: 1

parts:
  Arduino_Mega_2560 = Arduino Mega 2560 (Rev3)
  MFC_16_Pin_Header = SO16w [chip_label=SO16w package=SO(w)]

nets:
  N1: Arduino_Mega_2560.A1, MFC_16_Pin_Header.2
  N2: Arduino_Mega_2560.3V3, MFC_16_Pin_Header.8
  N3: MFC_16_Pin_Header.1, MFC_16_Pin_Header.3, MFC_16_Pin_Header.5, MFC_16_Pin_Header.10
